// Logisim project d_latch.circ as structural Verilog: 1 circuit, main circuit main
module main (
  input  D,
  input  EN,
  output Q,
  output NQ
);

  wire nand_1_out, nand_2_out, not_1_out;

  not not_1 (not_1_out, D);
  nand nand_1 (nand_1_out, D, EN);
  nand nand_2 (nand_2_out, EN, not_1_out);
  nand nand_3 (Q, nand_1_out, NQ);
  nand nand_4 (NQ, Q, nand_2_out);
endmodule
