// Logisim project jk_flipflop.circ as structural Verilog: 1 circuit, main circuit main
module main (
  input  J,
  input  K,
  input  CLK,
  output Q,
  output NQ
);

  wire nand_1_out, nand_2_out, nand_3_out, nand_4_out, nand_5_out, nand_6_out, nand_7_out, nand_8_out,
       nand_9_out, not_1_out, not_2_out, not_3_out, not_4_out;

  not not_1 (not_1_out, K);
  nand nand_1 (nand_1_out, J, NQ);
  nand nand_2 (nand_2_out, Q, not_1_out);
  nand nand_3 (nand_3_out, nand_1_out, nand_2_out);
  not not_2 (not_2_out, CLK);
  not not_3 (not_3_out, nand_3_out);
  nand nand_4 (nand_4_out, nand_3_out, not_2_out);
  nand nand_5 (nand_5_out, not_2_out, not_3_out);
  nand nand_6 (nand_6_out, nand_4_out, nand_7_out);
  nand nand_7 (nand_7_out, nand_6_out, nand_5_out);
  not not_4 (not_4_out, nand_6_out);
  nand nand_8 (nand_8_out, nand_6_out, CLK);
  nand nand_9 (nand_9_out, CLK, not_4_out);
  nand nand_10 (Q, nand_8_out, NQ);
  nand nand_11 (NQ, Q, nand_9_out);
endmodule
