// Logisim project d_flipflop_sc.circ as structural Verilog: 1 circuit, main circuit main
module main (
  input  D,
  input  CLK,
  input  SET,
  input  CLR,
  output Q,
  output NQ
);

  wire nand_2_out, nand_3_out, nand_4_out, nand_5_out, nand_6_out, nand_7_out, nCLR, not_1_out, not_3_out,
       not_4_out, nPRE;

  not not_1 (not_1_out, CLK);
  not not_2 (nCLR, CLR);
  not not_3 (not_3_out, D);
  nand nand_1 (nPRE, SET, nCLR);
  nand nand_2 (nand_2_out, D, nCLR, not_1_out);
  nand nand_3 (nand_3_out, not_1_out, nPRE, not_3_out);
  nand nand_4 (nand_4_out, nand_2_out, nPRE, nand_5_out);
  nand nand_5 (nand_5_out, nand_4_out, nCLR, nand_3_out);
  not not_4 (not_4_out, nand_4_out);
  nand nand_6 (nand_6_out, nand_4_out, nCLR, CLK);
  nand nand_7 (nand_7_out, CLK, nPRE, not_4_out);
  nand nand_8 (Q, nand_6_out, nPRE, NQ);
  nand nand_9 (NQ, Q, nCLR, nand_7_out);
endmodule
